// Logisim project Laplace32BitAccelerator-FPGA-TESTING.circ as structural Verilog: 7 circuits, main circuit main
module main (
  input  Reset,
  input  VonNeumann,
  output [3:0] TEST_OUT
);

  wire Clk_out;
  wire [31:0] BoundaryCell_1_gc_val, BoundaryCell_2_gc_val, BoundaryCell_3_gc_val, BoundaryCell_4_gc_val,
       BoundaryCell_5_gc_val, BoundaryCell_6_gc_val, BoundaryCell_7_gc_val, BoundaryCell_8_gc_val,
       BoundaryCell_9_gc_val, BoundaryCell_10_gc_val, BoundaryCell_11_gc_val, BoundaryCell_12_gc_val,
       BoundaryCell_13_gc_val, BoundaryCell_14_gc_val, BoundaryCell_15_gc_val, BoundaryCell_16_gc_val,
       BoundaryCell_17_gc_val, BoundaryCell_18_gc_val, BoundaryCell_19_gc_val, BoundaryCell_20_gc_val,
       gridcell_1_gc_val, gridcell_2_gc_val, gridcell_3_gc_val, gridcell_4_gc_val, gridcell_5_gc_val,
       gridcell_6_gc_val, gridcell_7_gc_val, gridcell_8_gc_val, gridcell_9_gc_val, gridcell_10_gc_val,
       gridcell_11_gc_val, gridcell_12_gc_val, gridcell_13_gc_val, gridcell_14_gc_val, gridcell_15_gc_val,
       gridcell_16_gc_val;

  Clock Clk (.out(Clk_out));
  BoundaryCell BoundaryCell_1 (
    .Reset(Reset), .Clk(Clk_out), .INIT_VAL({32{1'b0}}), .NEXT_VAL(gridcell_1_gc_val),
    .VonNeumann(VonNeumann), .GC_VAL(BoundaryCell_1_gc_val));
  BoundaryCell BoundaryCell_7 (
    .Reset(Reset), .Clk(Clk_out), .INIT_VAL({32{1'b0}}), .NEXT_VAL(gridcell_1_gc_val),
    .VonNeumann(VonNeumann), .GC_VAL(BoundaryCell_7_gc_val));
  BoundaryCell BoundaryCell_9 (
    .Reset(Reset), .Clk(Clk_out), .INIT_VAL({32{1'b0}}), .NEXT_VAL(gridcell_5_gc_val),
    .VonNeumann(VonNeumann), .GC_VAL(BoundaryCell_9_gc_val));
  BoundaryCell BoundaryCell_11 (
    .Reset(Reset), .Clk(Clk_out), .INIT_VAL({32{1'b0}}), .NEXT_VAL(gridcell_9_gc_val),
    .VonNeumann(VonNeumann), .GC_VAL(BoundaryCell_11_gc_val));
  BoundaryCell BoundaryCell_13 (
    .Reset(Reset), .Clk(Clk_out), .INIT_VAL({32{1'b0}}), .NEXT_VAL(gridcell_13_gc_val),
    .VonNeumann(VonNeumann), .GC_VAL(BoundaryCell_13_gc_val));
  BoundaryCell BoundaryCell_15 (
    .Reset(Reset), .Clk(Clk_out), .INIT_VAL({32{1'b0}}), .NEXT_VAL(gridcell_13_gc_val),
    .VonNeumann(VonNeumann), .GC_VAL(BoundaryCell_15_gc_val));
  BoundaryCell BoundaryCell_2 (
    .Reset(Reset), .Clk(Clk_out), .INIT_VAL({32{1'b0}}), .NEXT_VAL(gridcell_1_gc_val),
    .VonNeumann(VonNeumann), .GC_VAL(BoundaryCell_2_gc_val));
  gridcell gridcell_1 (
    .Reset(Reset), .Clk(Clk_out), .VAL({32{1'b0}}), .IN01(BoundaryCell_2_gc_val), .IN10(gridcell_2_gc_val),
    .IN0NEG1(gridcell_5_gc_val), .INNEG10(BoundaryCell_7_gc_val), .ERR_TOL(32'h10), .MIN_TOL(32'h1),
    .GC_VAL(gridcell_1_gc_val));
  gridcell gridcell_5 (
    .Reset(Reset), .Clk(Clk_out), .VAL({32{1'b0}}), .IN01(gridcell_1_gc_val), .IN10(gridcell_6_gc_val),
    .IN0NEG1(gridcell_9_gc_val), .INNEG10(BoundaryCell_9_gc_val), .ERR_TOL(32'h10), .MIN_TOL(32'h1),
    .GC_VAL(gridcell_5_gc_val));
  gridcell gridcell_9 (
    .Reset(Reset), .Clk(Clk_out), .VAL({32{1'b0}}), .IN01(gridcell_5_gc_val), .IN10(gridcell_10_gc_val),
    .IN0NEG1(gridcell_13_gc_val), .INNEG10(BoundaryCell_11_gc_val), .ERR_TOL(32'h10), .MIN_TOL(32'h1),
    .GC_VAL(gridcell_9_gc_val));
  gridcell gridcell_13 (
    .Reset(Reset), .Clk(Clk_out), .VAL({32{1'b0}}), .IN01(gridcell_9_gc_val), .IN10(gridcell_14_gc_val),
    .IN0NEG1(BoundaryCell_16_gc_val), .INNEG10(BoundaryCell_13_gc_val), .ERR_TOL(32'h10), .MIN_TOL(32'h1),
    .GC_VAL(gridcell_13_gc_val));
  BoundaryCell BoundaryCell_16 (
    .Reset(Reset), .Clk(Clk_out), .INIT_VAL({32{1'b0}}), .NEXT_VAL(gridcell_13_gc_val),
    .VonNeumann(VonNeumann), .GC_VAL(BoundaryCell_16_gc_val));
  BoundaryCell BoundaryCell_3 (
    .Reset(Reset), .Clk(Clk_out), .INIT_VAL({32{1'b0}}), .NEXT_VAL(gridcell_2_gc_val),
    .VonNeumann(VonNeumann), .GC_VAL(BoundaryCell_3_gc_val));
  gridcell gridcell_2 (
    .Reset(Reset), .Clk(Clk_out), .VAL({32{1'b0}}), .IN01(BoundaryCell_3_gc_val), .IN10(gridcell_3_gc_val),
    .IN0NEG1(gridcell_6_gc_val), .INNEG10(gridcell_1_gc_val), .ERR_TOL(32'h10), .MIN_TOL(32'h1),
    .GC_VAL(gridcell_2_gc_val));
  gridcell gridcell_6 (
    .Reset(Reset), .Clk(Clk_out), .VAL({32{1'b0}}), .IN01(gridcell_2_gc_val), .IN10(gridcell_7_gc_val),
    .IN0NEG1(gridcell_10_gc_val), .INNEG10(gridcell_5_gc_val), .ERR_TOL(32'h10), .MIN_TOL(32'h1),
    .GC_VAL(gridcell_6_gc_val));
  gridcell gridcell_10 (
    .Reset(Reset), .Clk(Clk_out), .VAL(32'h10000), .IN01(gridcell_6_gc_val), .IN10(gridcell_11_gc_val),
    .IN0NEG1(gridcell_14_gc_val), .INNEG10(gridcell_9_gc_val), .ERR_TOL(32'h10), .MIN_TOL(32'h1),
    .GC_VAL(gridcell_10_gc_val));
  gridcell gridcell_14 (
    .Reset(Reset), .Clk(Clk_out), .VAL({32{1'b0}}), .IN01(gridcell_10_gc_val), .IN10(gridcell_15_gc_val),
    .IN0NEG1(BoundaryCell_17_gc_val), .INNEG10(gridcell_13_gc_val), .ERR_TOL(32'h10), .MIN_TOL(32'h1),
    .GC_VAL(gridcell_14_gc_val));
  BoundaryCell BoundaryCell_17 (
    .Reset(Reset), .Clk(Clk_out), .INIT_VAL({32{1'b0}}), .NEXT_VAL(gridcell_14_gc_val),
    .VonNeumann(VonNeumann), .GC_VAL(BoundaryCell_17_gc_val));
  Bit_Extender #(.in_width(32), .out_width(4)) bit_extender_1 (.in(gridcell_10_gc_val), .out(TEST_OUT));
  BoundaryCell BoundaryCell_4 (
    .Reset(Reset), .Clk(Clk_out), .INIT_VAL({32{1'b0}}), .NEXT_VAL(gridcell_3_gc_val),
    .VonNeumann(VonNeumann), .GC_VAL(BoundaryCell_4_gc_val));
  gridcell gridcell_3 (
    .Reset(Reset), .Clk(Clk_out), .VAL({32{1'b0}}), .IN01(BoundaryCell_4_gc_val), .IN10(gridcell_4_gc_val),
    .IN0NEG1(gridcell_7_gc_val), .INNEG10(gridcell_2_gc_val), .ERR_TOL(32'h10), .MIN_TOL(32'h1),
    .GC_VAL(gridcell_3_gc_val));
  gridcell gridcell_7 (
    .Reset(Reset), .Clk(Clk_out), .VAL({32{1'b0}}), .IN01(gridcell_3_gc_val), .IN10(gridcell_8_gc_val),
    .IN0NEG1(gridcell_11_gc_val), .INNEG10(gridcell_6_gc_val), .ERR_TOL(32'h10), .MIN_TOL(32'h1),
    .GC_VAL(gridcell_7_gc_val));
  gridcell gridcell_11 (
    .Reset(Reset), .Clk(Clk_out), .VAL({32{1'b0}}), .IN01(gridcell_7_gc_val), .IN10(gridcell_12_gc_val),
    .IN0NEG1(gridcell_15_gc_val), .INNEG10(gridcell_11_gc_val), .ERR_TOL(32'h10), .MIN_TOL(32'h1),
    .GC_VAL(gridcell_11_gc_val));
  gridcell gridcell_15 (
    .Reset(Reset), .Clk(Clk_out), .VAL({32{1'b0}}), .IN01(gridcell_11_gc_val), .IN10(gridcell_16_gc_val),
    .IN0NEG1(BoundaryCell_18_gc_val), .INNEG10(gridcell_14_gc_val), .ERR_TOL(32'h10), .MIN_TOL(32'h1),
    .GC_VAL(gridcell_15_gc_val));
  BoundaryCell BoundaryCell_18 (
    .Reset(Reset), .Clk(Clk_out), .INIT_VAL({32{1'b0}}), .NEXT_VAL(gridcell_15_gc_val),
    .VonNeumann(VonNeumann), .GC_VAL(BoundaryCell_18_gc_val));
  BoundaryCell BoundaryCell_5 (
    .Reset(Reset), .Clk(Clk_out), .INIT_VAL({32{1'b0}}), .NEXT_VAL(gridcell_4_gc_val),
    .VonNeumann(VonNeumann), .GC_VAL(BoundaryCell_5_gc_val));
  gridcell gridcell_4 (
    .Reset(Reset), .Clk(Clk_out), .VAL({32{1'b0}}), .IN01(BoundaryCell_5_gc_val),
    .IN10(BoundaryCell_8_gc_val), .IN0NEG1(gridcell_8_gc_val), .INNEG10(gridcell_3_gc_val), .ERR_TOL(32'h10),
    .MIN_TOL(32'h1), .GC_VAL(gridcell_4_gc_val));
  gridcell gridcell_8 (
    .Reset(Reset), .Clk(Clk_out), .VAL({32{1'b0}}), .IN01(gridcell_4_gc_val), .IN10(BoundaryCell_10_gc_val),
    .IN0NEG1(gridcell_12_gc_val), .INNEG10(gridcell_7_gc_val), .ERR_TOL(32'h10), .MIN_TOL(32'h1),
    .GC_VAL(gridcell_8_gc_val));
  gridcell gridcell_12 (
    .Reset(Reset), .Clk(Clk_out), .VAL({32{1'b0}}), .IN01(gridcell_8_gc_val), .IN10(BoundaryCell_12_gc_val),
    .IN0NEG1(gridcell_16_gc_val), .INNEG10(gridcell_11_gc_val), .ERR_TOL(32'h10), .MIN_TOL(32'h1),
    .GC_VAL(gridcell_12_gc_val));
  gridcell gridcell_16 (
    .Reset(Reset), .Clk(Clk_out), .VAL({32{1'b0}}), .IN01(gridcell_12_gc_val), .IN10(BoundaryCell_14_gc_val),
    .IN0NEG1(BoundaryCell_19_gc_val), .INNEG10(gridcell_15_gc_val), .ERR_TOL(32'h10), .MIN_TOL(32'h1),
    .GC_VAL(gridcell_16_gc_val));
  BoundaryCell BoundaryCell_19 (
    .Reset(Reset), .Clk(Clk_out), .INIT_VAL({32{1'b0}}), .NEXT_VAL(gridcell_16_gc_val),
    .VonNeumann(VonNeumann), .GC_VAL(BoundaryCell_19_gc_val));
  BoundaryCell BoundaryCell_6 (
    .Reset(Reset), .Clk(Clk_out), .INIT_VAL({32{1'b0}}), .NEXT_VAL(gridcell_4_gc_val),
    .VonNeumann(VonNeumann), .GC_VAL(BoundaryCell_6_gc_val));
  BoundaryCell BoundaryCell_8 (
    .Reset(Reset), .Clk(Clk_out), .INIT_VAL({32{1'b0}}), .NEXT_VAL(gridcell_4_gc_val),
    .VonNeumann(VonNeumann), .GC_VAL(BoundaryCell_8_gc_val));
  BoundaryCell BoundaryCell_10 (
    .Reset(Reset), .Clk(Clk_out), .INIT_VAL({32{1'b0}}), .NEXT_VAL(gridcell_8_gc_val),
    .VonNeumann(VonNeumann), .GC_VAL(BoundaryCell_10_gc_val));
  BoundaryCell BoundaryCell_12 (
    .Reset(Reset), .Clk(Clk_out), .INIT_VAL({32{1'b0}}), .NEXT_VAL(gridcell_12_gc_val),
    .VonNeumann(VonNeumann), .GC_VAL(BoundaryCell_12_gc_val));
  BoundaryCell BoundaryCell_14 (
    .Reset(Reset), .Clk(Clk_out), .INIT_VAL({32{1'b0}}), .NEXT_VAL(gridcell_16_gc_val),
    .VonNeumann(VonNeumann), .GC_VAL(BoundaryCell_14_gc_val));
  BoundaryCell BoundaryCell_20 (
    .Reset(Reset), .Clk(Clk_out), .INIT_VAL({32{1'b0}}), .NEXT_VAL(gridcell_16_gc_val),
    .VonNeumann(VonNeumann), .GC_VAL(BoundaryCell_20_gc_val));
endmodule

module gridcellREGALU (
  input  Reset,
  input  Load,
  input  Shift,
  input  Clk,
  input  [31:0] VAL,
  input  [31:0] IN01,
  input  [31:0] IN10,
  input  [31:0] IN0NEG1,
  input  [31:0] INNEG10,
  output [31:0] NEW_VAL,
  output [31:0] OLD_VAL
);

  wire [31:0] shift_register_1_p5;

  // Shift_Register #(.length(2), .width(32)) shift_register_1: pin names not known; wires that end beside it: Reset, Load, Shift, Clk, shift_register_1_p5, VAL, NEW_VAL, NEW_VAL, OLD_VAL
  cellALU cellALUlolol (.IN01(IN01), .IN10(IN10), .IN0NEG1(IN0NEG1), .INNEG10(INNEG10), .NEW_VAL(shift_register_1_p5));
endmodule

module cellALU (
  input  [31:0] IN01,
  input  [31:0] IN10,
  input  [31:0] IN0NEG1,
  input  [31:0] INNEG10,
  output [31:0] NEW_VAL
);

  wire [31:0] adder_1_out, adder_2_out, adder_3_out;

  Adder #(.width(32)) adder_1 (.a(IN01), .b(IN10), .out(adder_1_out));  // open: cin, cout
  Adder #(.width(32)) adder_2 (.a(IN0NEG1), .b(INNEG10), .out(adder_2_out));  // open: cin, cout
  Adder #(.width(32)) adder_3 (.a(adder_1_out), .b(adder_2_out), .out(adder_3_out));  // open: cin, cout
  Shifter #(.shift("lr"), .width(32)) shifter_1 (.in(adder_3_out), .\dist (5'b00010), .out(NEW_VAL));
endmodule

module cellFSM (
  input  Reset,
  input  CONV_FLAG,
  input  Clk,
  output Load,
  output Shift
);

  D_Flip_Flop d_ff_1 (.D(Reset), .clk(Clk), .Q(Load));  // open: Qn, preset, reset
  nor nor_1 (Shift, Reset, CONV_FLAG);
endmodule

module ConvergenceChecker (
  input  [31:0] OLD_VAL,
  input  [31:0] NEW_VAL,
  input  [31:0] ERR_TOL,
  input  [31:0] MIN_TOL,
  output CONV_FLAG
);

  wire comparator_1_lt, comparator_2_gt;
  wire [32:0] bit_extender_1_out, bit_extender_2_out, subtractor_1_out;

  assign bit_extender_1_out = {{1{1'b0}}, OLD_VAL};  // Bit_Extender bit_extender_1
  assign bit_extender_2_out = {{1{1'b0}}, NEW_VAL};  // Bit_Extender bit_extender_2
  Subtractor #(.width(33)) subtractor_1 (
    .a(bit_extender_1_out), .b(bit_extender_2_out), .out(subtractor_1_out));  // open: bin, bout
  Comparator #(.width(32)) comparator_1 (
    .a(subtractor_1_out[31:0]), .b(ERR_TOL), .lt(comparator_1_lt));  // open: gt, eq
  Comparator #(.width(32)) comparator_2 (
    .a(subtractor_1_out[31:0]), .b(MIN_TOL), .gt(comparator_2_gt));  // open: eq, lt
  and and_1 (CONV_FLAG, comparator_1_lt, comparator_2_gt);
endmodule

module gridcell (
  input  Reset,
  input  Clk,
  input  [31:0] VAL,
  input  [31:0] IN01,
  input  [31:0] IN10,
  input  [31:0] IN0NEG1,
  input  [31:0] INNEG10,
  input  [31:0] ERR_TOL,
  input  [31:0] MIN_TOL,
  output [31:0] GC_VAL
);

  wire cellFSM_1_load, cellFSM_1_shift, ConvergenceChecker_1_conv_flag;
  wire [31:0] gridcellREGALU_1_old_val;

  gridcellREGALU gridcellREGALU_1 (
    .Reset(Reset), .Load(cellFSM_1_load), .Shift(cellFSM_1_shift), .Clk(Clk), .VAL(VAL), .IN01(IN01),
    .IN10(IN10), .IN0NEG1(IN0NEG1), .INNEG10(INNEG10), .NEW_VAL(GC_VAL), .OLD_VAL(gridcellREGALU_1_old_val));
  cellFSM cellFSM_1 (
    .Reset(Reset), .CONV_FLAG(ConvergenceChecker_1_conv_flag), .Clk(Clk), .Load(cellFSM_1_load),
    .Shift(cellFSM_1_shift));
  ConvergenceChecker ConvergenceChecker_1 (
    .OLD_VAL(gridcellREGALU_1_old_val), .NEW_VAL(GC_VAL), .ERR_TOL(ERR_TOL), .MIN_TOL(MIN_TOL),
    .CONV_FLAG(ConvergenceChecker_1_conv_flag));
endmodule

module BoundaryCell (
  input  Reset,
  input  Clk,
  input  [31:0] INIT_VAL,
  input  [31:0] NEXT_VAL,
  input  VonNeumann,
  output [31:0] GC_VAL
);

  wire [31:0] shift_register_1_p4;

  // Shift_Register #(.length(1), .width(32)) shift_register_1: pin names not known; wires that end beside it: Reset, 1'b1, Clk, shift_register_1_p4, GC_VAL
  Multiplexer #(.width(32)) multiplexer_1 (.in0(INIT_VAL), .in1(NEXT_VAL), .out(shift_register_1_p4), .sel(VonNeumann));
endmodule
